# Fritzing sketch Final PCB v1 (saved by Fritzing 0.9.4)
circuit board: 8.46667cm x 5.64444cm
breadboards: 1

parts:
  Raspberry_Pi_4 = Raspberry Pi 3 [part_number=RPI-3-V1.2]
  JP1 = Header 3 [package=screwterminal-3.5mm-3_lock.007s]  # not connected
  Part1 = Adafruit PCA9685 PWM/Servo Breakout [part_number=815]
  Part2 = Adafruit VCNL4010 Proximity and Light sensor [part_number="Adafruit #466"]
  JP2 = Header 4 [package=screwterminal-3.5mm-4_lock]  # not connected

nets:
  N1: Raspberry_Pi_4.GPIO2, Part1.SDA, Part2.SDA
  N2: Raspberry_Pi_4.GPIO3, Part1.SCL, Part2.SCL

custom parts:
  Adafruit PCA9685 PWM/Servo Breakout: Using only two pins, control 16 free-running PWM outputs! I2C-controlled PWM driver with a built in clock. Unlike the TLC5940 family, you do not need to continuously send it signal tying up your microcontroller, its completely free running! 5V compliant, which means you can control it from a 3.3V microcontroller and still safely drive up to 6V outputs (this is good for when you want to control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
  Adafruit VCNL4010 Proximity and Light sensor: The VCNL4010 sensor is a nice way to add a small-distance proximity sensor to your microcontroller project. For longer distances (in the range of cm, you can use a SHARP IR distance sensor, but those are only good if the object is over 10 cm away. The VCNL4010 is designed for much shorter distances, no more than 200mm (about 7.5") and under our experimentation we found it worked best at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
