# Fritzing sketch Final PCB v3(Shortened) (saved by Fritzing 0.9.4)
circuit board: 7.17124cm x 5.63584cm
breadboards: 1

parts:
  Raspberry_Pi_4 = Raspberry Pi 3 [part_number=RPI-3-V1.2]
  Part2 = Adafruit VCNL4010 Proximity and Light sensor [part_number="Adafruit #466"]
  IR1 = TSOP312.., 314.. [package=THT]
  JP2 = Header 4 [package=molex-1x4_lock]
  Part1 = Adafruit PCA9685 PWM/Servo Breakout [part_number=815]

nets:
  3V3: Raspberry_Pi_4.3v3, Raspberry_Pi_4.3V3, Part2.VIN, JP2.4, Part1.VCC
  N1: Raspberry_Pi_4.GPIO2, Part2.SDA, JP2.2, Part1.SDA
  N2: Raspberry_Pi_4.GPIO3, Part2.SCL, JP2.3, Part1.SCL
  GND: Raspberry_Pi_4.GND, Part2.GND, IR1.GND, JP2.1, Part1.GND
  N3: Raspberry_Pi_4.ID_SD, IR1.Data
  N4: Raspberry_Pi_4.5V, IR1.Vs

custom parts:
  Adafruit VCNL4010 Proximity and Light sensor: The VCNL4010 sensor is a nice way to add a small-distance proximity sensor to your microcontroller project. For longer distances (in the range of cm, you can use a SHARP IR distance sensor, but those are only good if the object is over 10 cm away. The VCNL4010 is designed for much shorter distances, no more than 200mm (about 7.5") and under our experimentation we found it worked best at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
  Adafruit PCA9685 PWM/Servo Breakout: Using only two pins, control 16 free-running PWM outputs! I2C-controlled PWM driver with a built in clock. Unlike the TLC5940 family, you do not need to continuously send it signal tying up your microcontroller, its completely free running! 5V compliant, which means you can control it from a 3.3V microcontroller and still safely drive up to 6V outputs (this is good for when you want to control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
