# Fritzing sketch IRBREAKBEAMSENSOR (saved by Fritzing 0.9.3b)
circuit board: 5.54583cm x 6.03902cm
breadboards: 1

parts:
  Transmitter = Header 3 [package=screwterminal-3.5mm-3_lock.007s]
  Receiver = Header 4 [package=screwterminal-3.5mm-4_lock]
  LED1 = smd LED [color="Red (633nm)" package="0805 [SMD]"]
  R2_4_7KOhm = Resistor [tolerance=±5% resistance=4.7k package=THT]
  R1_1KOhm = Resistor [tolerance=±20% resistance=1k package=THT]
  Raspberry_Pi_1 = Raspberry Pi 3 [part_number=RPI-3-V1.2]

nets:
  3V3: Transmitter.1, Receiver.1, R2_4_7KOhm.Pin_1, R1_1KOhm.Pin_1, Raspberry_Pi_1.3v3, Raspberry_Pi_1.3V3
  N1: Transmitter.3, Receiver.2, Raspberry_Pi_1.GND
  N2: Receiver.3, LED1.cathode, R2_4_7KOhm.Pin_0, Raspberry_Pi_1.GPIO17
  N3: LED1.anode, R1_1KOhm.Pin_0

notes:
  Reciever connections:
  1= Power
  2 = Ground
  3 = Output
  Transmitter connections:
  3 = Ground
  1 = Power
  George Alexandris
