# Fritzing sketch Vikas_VCNL4010ProximityPCBFINAL (saved by Fritzing 0.9.3b)
circuit board: 6.35cm x 5.7cm
breadboards: 1

parts:
  Proximity_Sensor = Adafruit VCNL4010 Proximity and Light sensor [part_number="Adafruit #466"]
  LED1 = RGB LED (com. anode, rbg) [package="5 mm [THT]"]
  Raspberry_Pi_4 = Raspberry Pi 3 [part_number=RPI-3-V1.2]
  R3 = Resistor [tolerance=±5% resistance=220 package=THT]
  R2 = Resistor [tolerance=±5% resistance=220 package=THT]
  R1 = Resistor [tolerance=±5% resistance=220 package=THT]

nets:
  N1: Proximity_Sensor.SDA, Raspberry_Pi_4.GPIO2
  N2: Proximity_Sensor.SCL, Raspberry_Pi_4.GPIO3
  GND: Proximity_Sensor.GND, Raspberry_Pi_4.GND
  VIN: Proximity_Sensor.VIN, LED1.common_anode, Raspberry_Pi_4.5V
  N3: LED1.red_cathode, R1.Pin_1
  N4: LED1.blue_cathode, R2.Pin_1
  N5: LED1.green_cathode, R3.Pin_1
  N6: Raspberry_Pi_4.GIPO17, R1.Pin_0
  N7: Raspberry_Pi_4.GIPO27, R3.Pin_0
  N8: Raspberry_Pi_4.GIPO18, R2.Pin_0

notes:
  Common Anode RGB LED(4 leads, 2nd lead connects to 5V on PI)
  Will be using a RPI 4 Model B(same GPIO pinouts as shown here)
  Vikas Sharma
  VIN
  SCL
  GND
  SDA
  Sensor: will use 3.3V leftover out of 5V, 3.3V after the 1st resistor(5V-1.7V=3.3V)
  Voltage will be divided between 3 (220 ohm) resistors.(using roughly 1.7V out of 5V)

custom parts:
  Adafruit VCNL4010 Proximity and Light sensor: The VCNL4010 sensor is a nice way to add a small-distance proximity sensor to your microcontroller project. For longer distances (in the range of cm, you can use a SHARP IR distance sensor, but those are only good if the object is over 10 cm away. The VCNL4010 is designed for much shorter distances, no more than 200mm (about 7.5") and under our experimentation we found it worked best at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
